# Fritzing sketch Proj. Grupo (saved by Fritzing 0.9.3b)
breadboards: 1

parts:
  Componente1 = Arduino Uno (Rev3)
  RHT1 = Humidity and Temperature Sensor RHT03
  J1 = Piezo Speaker
  LED1 = LED - 5mm [color="Green (570nm)" package="5 mm [THT]"]
  LED2 = LED - 5mm [color="Red (633nm)" package="5 mm [THT]"]
  R1 = Resistor [tolerance=±5% resistance=220 package=THT]
  R2 = Resistor [tolerance=±5% resistance=220 package=THT]

nets:
  N1: Componente1.A1, RHT1.GND_1
  N2: Componente1.D6_PWM, R1.Pin_0
  N3: Componente1.D7, R2.Pin_0
  5V: Componente1.5V, RHT1.Vcc
  N4: Componente1.GND, RHT1.GND_2, J1.pin1, LED1.cathode, LED2.cathode
  N5: LED1.anode, R2.Pin_1
  N6: LED2.anode, R1.Pin_1

notes:
  SENSOR PIR
