# Fritzing sketch Untitled Sketch 2 (saved by Fritzing 0.9.3b)
breadboards: 1

parts:
  S1 = KY-026
  SW-1 = Vibration sensor module
  J1 = Piezo Speaker
  R1 = Resistor [tolerance=±5% resistance=220 package=THT]
  LED1 = LED - 5mm [color="Red (633nm)" package="5 mm [THT]"]
  Componente1 = Arduino Uno (Rev3)

nets:
  N1: S1.pin1, Componente1.D7
  N2: S1.pin2, SW-1.Ground, J1.pin1, LED1.cathode, Componente1.GND
  VCC: S1.pin3, SW-1.vcc, Componente1.5V
  N3: S1.pin4, Componente1.A1
  N4: SW-1.Digital_output, Componente1.D3_PWM
  N5: J1.pin2, Componente1.D2
  N6: R1.Pin_0, LED1.anode
  N7: R1.Pin_1, Componente1.D6_PWM

custom parts:
  KY-026: ky-026 flame sensor module
  Vibration sensor module: Single-roller type full induction trigger switch. When no vibration or tilt, the product is ON conduction state, and in the steady state, when a vibration or tilt, the switch will be rendered instantly disconnect the conductive resistance increases, generating a current pulse signal, thereby triggering circuit. The default state of the swith is close Digital output Supply voltage:3.3V-5V On-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
